// Logisim project tmp2.circ as structural Verilog: 1 circuit, main circuit main
module main (
  input  [3:0] in_1,
  output [6:0] out_2
);

  wire decoder_1_out0, decoder_1_out1, decoder_1_out2, decoder_1_out3, decoder_1_out4, decoder_1_out5,
       decoder_1_out6, decoder_1_out7, decoder_1_out8, decoder_1_out9, or_1_out, or_2_out, or_3_out,
       or_4_out, or_6_out;

  Decoder #(.select(4)) decoder_1 (
    .out0(decoder_1_out0), .out1(decoder_1_out1), .out2(decoder_1_out2), .out3(decoder_1_out3),
    .out4(decoder_1_out4), .out5(decoder_1_out5), .out6(decoder_1_out6), .out7(decoder_1_out7),
    .out8(decoder_1_out8), .out9(decoder_1_out9), .sel(in_1));  // open: out10, out11, out12, out13, out14, out15, en
  or or_1 (or_1_out, decoder_1_out1, decoder_1_out4);
  or or_2 (or_2_out, decoder_1_out5, decoder_1_out6);
  not not_1 (out_2[5], or_2_out);
  not not_2 (out_2[6], or_1_out);
  or or_3 (or_3_out, decoder_1_out1, decoder_1_out4, decoder_1_out7);
  not not_3 (out_2[4], decoder_1_out2);
  not not_4 (out_2[3], or_3_out);
  or or_4 (or_4_out, decoder_1_out1, decoder_1_out2, decoder_1_out3, decoder_1_out7);
  or or_5 (out_2[2], decoder_1_out0, decoder_1_out2, decoder_1_out6, decoder_1_out8);
  not not_5 (out_2[1], or_4_out);
  or or_6 (or_6_out, decoder_1_out0, decoder_1_out1, decoder_1_out7);
  not not_6 (out_2[0], or_6_out);
endmodule
