// Logisim project tmp3.circ as structural Verilog: 1 circuit, main circuit main
module main (
  input  [2:0] in_1,
  output out_2
);

  wire and_1_out, not_1_out, or_1_out;

  and and_1 (and_1_out, in_1[0], in_1[1], in_1[2]);
  or or_1 (or_1_out, in_1[0], in_1[1], in_1[2]);
  not not_1 (not_1_out, or_1_out);
  or or_2 (out_2, and_1_out, not_1_out);
endmodule
