// Logisim project tmp4.circ as structural Verilog: 1 circuit, main circuit main
module main (
  input  [3:0] in_1,
  output out_2
);

  wire and_1_out, and_2_out, or_1_out;

  and and_1 (and_1_out, in_1[0], in_1[2]);
  and and_2 (and_2_out, in_1[1], in_1[3]);
  not not_1 (out_2, or_1_out);
  or or_1 (or_1_out, and_1_out, and_2_out);
endmodule
