// Logisim project tmp2.circ as structural Verilog: 1 circuit, main circuit main
module main (
  input  in_1,
  input  in_2,
  output out_3
);

  wire shift_register_1_q0, shift_register_1_q1, shift_register_1_q3, shift_register_1_q4, xnor_1_out,
       xnor_2_out;

  Shift_Register #(.length(5)) shift_register_1 (
    .shift(1'b1), .in(in_1), .clk(in_2), .q0(shift_register_1_q0), .q1(shift_register_1_q1),
    .q3(shift_register_1_q3), .q4(shift_register_1_q4));  // open: out, load, clr, d0, d1, d2, q2, d3, d4
  xnor xnor_1 (xnor_1_out, shift_register_1_q4, shift_register_1_q0);
  and and_1 (out_3, xnor_1_out, xnor_2_out);
  xnor xnor_2 (xnor_2_out, shift_register_1_q1, shift_register_1_q3);
endmodule
